// Logisim project FINAL (1).circ as structural Verilog
module main (
  input  anulare_prespalare,
  input  anulare_clatire,
  input  in_3,
  input  in_4,
  input  in_5,
  input  in_6,
  input  in_7,
  input  in_8,
  input  in_9,
  input  in_10,
  input  in_11,
  input  in_12,
  input  in_13,
  input  in_14,
  input  in_15,
  input  in_16,
  input  in_17,
  input  in_18,
  input  in_19,
  input  Start,
  input  in_21
);

  wire and_gate_1_c, clock_1_out, not_gate_1_o, not_gate_2_o, or_gate_1_rez, program_1_alimentaree,
       program_1_centrifugaree, program_1_clatiree, program_1_evacuaree, program_1_finn,
       program_1_incalziree, program_1_prespalaree, program_1_spalaree, program_1_usablocataa, starter_1_ok;
  wire [6:0] sevensegmentdecoder_1_minute, sevensegmentdecoder_1_minutes, sevensegmentdecoder_1_second,
       sevensegmentdecoder_1_seconds;
  wire [8:0] buttons_1_v, registrubuttons_1_q;
  wire [12:0] adder12bits_1_rez, counter13_1_q, loader_1_v, mux_4to1_1_o, registru_1_q;
  wire [15:0] time_convert_1_output;

  Clock clock_1 (.out(clock_1_out));
  BUTTONS buttons_1 (
    .Anulare_prespalare(anulare_prespalare), .ANulare_clatire(anulare_clatire), .reset(in_3), .MANUAL(in_4),
    .t30(in_5), .t40(in_6), .t60(in_7), .t90(in_8), .r800(in_9), .r1000(in_10), .r1200(in_11),
    .SPALARE_RAPIDA(in_12), .CAMASI(in_13), .ANTIALERGIC(in_14), .CULORI_INCHISE(in_15),
    .RUFE_MURDARE(in_16), .DOOR(in_17), .prespalare(in_18), .clatire(in_19), .v(buttons_1_v));
  loader loader_1 (
    .reset(in_3), .t30(in_5), .t40(in_6), .t60(in_7), .t90(in_8), .SPALARE_RAPIDA(in_12), .CAMASI(in_13),
    .ANTIALERGIC(in_14), .CULORI_INCHISE(in_15), .RUFE_MURDARE(in_16), .DOOR(in_17), .v(loader_1_v));
  mux_4to1 mux_4to1_1 (.sel0(registrubuttons_1_q[0]), .sel1(registrubuttons_1_q[1]), .o(mux_4to1_1_o));
  RegistruButtons registrubuttons_1 (.load(1'b1), .clk(clock_1_out), .data(buttons_1_v), .q(registrubuttons_1_q));
  Registru registru_1 (.load(1'b1), .clk(clock_1_out), .data(loader_1_v), .q(registru_1_q));
  Adder12Bits adder12bits_1 (.A(mux_4to1_1_o), .B(registru_1_q), .rez(adder12bits_1_rez));
  LED led_1 (.in(registrubuttons_1_q[0]));
  LED led_2 (.in(registrubuttons_1_q[1]));
  LED led_3 (.in(registrubuttons_1_q[2]));
  LED led_4 (.in(registrubuttons_1_q[3]));
  LED led_5 (.in(registrubuttons_1_q[4]));
  LED led_6 (.in(registrubuttons_1_q[5]));
  LED led_7 (.in(registrubuttons_1_q[6]));
  LED led_8 (.in(registrubuttons_1_q[7]));
  LED led_9 (.in(registrubuttons_1_q[8]));
  not_gate not_gate_1 (.i(starter_1_ok), .o(not_gate_1_o));
  Counter13 counter13_1 (
    .Load(not_gate_1_o), .Clk_EN(starter_1_ok), .CLK(clock_1_out), .RST(in_21), .Data(adder12bits_1_rez),
    .Q(counter13_1_q));
  starter starter_1 (
    .RESET(in_3), .t30(registrubuttons_1_q[8]), .t40(registrubuttons_1_q[7]), .t60(registrubuttons_1_q[6]),
    .t90(registrubuttons_1_q[5]), .r800(registrubuttons_1_q[4]), .r1000(registrubuttons_1_q[3]),
    .r1200(registrubuttons_1_q[2]), .START(Start), .DOOR(in_17), .Ok(starter_1_ok));
  SevenSegmentDecoder sevensegmentdecoder_1 (
    .Input(time_convert_1_output), .second(sevensegmentdecoder_1_second),
    .seconds(sevensegmentdecoder_1_seconds), .minute(sevensegmentdecoder_1_minute),
    .minutes(sevensegmentdecoder_1_minutes));
  time_convert time_convert_1 (.\input (counter13_1_q), .\output (time_convert_1_output));
  Program program_1 (
    .v0(registrubuttons_1_q[0]), .v1(registrubuttons_1_q[0]), .v5(registrubuttons_1_q[8]),
    .v6(registrubuttons_1_q[7]), .v7(registrubuttons_1_q[6]), .v8(registrubuttons_1_q[5]), .rst(in_3),
    .ok(starter_1_ok), .clock(clock_1_out), .finn(program_1_finn), .UsaBlocataa(program_1_usablocataa),
    .clatiree(program_1_clatiree), .spalaree(program_1_spalaree), .prespalaree(program_1_prespalaree),
    .evacuaree(program_1_evacuaree), .incalziree(program_1_incalziree),
    .centrifugaree(program_1_centrifugaree), .alimentaree(program_1_alimentaree));
  LED led_10 (.in(program_1_clatiree));
  LED led_11 (.in(program_1_spalaree));
  LED led_12 (.in(program_1_prespalaree));
  LED led_13 (.in(program_1_evacuaree));
  LED led_14 (.in(program_1_incalziree));
  LED led_15 (.in(program_1_centrifugaree));
  LED led_16 (.in(program_1_alimentaree));
  _7_Segment_Display u_7_segment_display_1 (
    .g(sevensegmentdecoder_1_second[0]), .f(sevensegmentdecoder_1_second[1]),
    .a(sevensegmentdecoder_1_second[6]), .b(sevensegmentdecoder_1_second[5]),
    .e(sevensegmentdecoder_1_second[2]), .d(sevensegmentdecoder_1_second[3]),
    .c(sevensegmentdecoder_1_second[4]));  // open: dp
  _7_Segment_Display u_7_segment_display_2 (
    .g(sevensegmentdecoder_1_seconds[0]), .f(sevensegmentdecoder_1_seconds[1]),
    .a(sevensegmentdecoder_1_seconds[6]), .b(sevensegmentdecoder_1_seconds[5]),
    .e(sevensegmentdecoder_1_seconds[2]), .d(sevensegmentdecoder_1_seconds[3]),
    .c(sevensegmentdecoder_1_seconds[4]));  // open: dp
  not_gate not_gate_2 (.i(program_1_finn), .o(not_gate_2_o));
  OR_gate or_gate_1 (.a(program_1_usablocataa), .b(starter_1_ok), .rez(or_gate_1_rez));  // open: c, d, e, f, g, h
  _7_Segment_Display u_7_segment_display_3 (
    .g(sevensegmentdecoder_1_minute[0]), .f(sevensegmentdecoder_1_minute[1]),
    .a(sevensegmentdecoder_1_minute[6]), .b(sevensegmentdecoder_1_minute[5]),
    .e(sevensegmentdecoder_1_minute[2]), .d(sevensegmentdecoder_1_minute[3]),
    .c(sevensegmentdecoder_1_minute[4]));  // open: dp
  _7_Segment_Display u_7_segment_display_4 (
    .g(sevensegmentdecoder_1_minutes[0]), .f(sevensegmentdecoder_1_minutes[1]),
    .a(sevensegmentdecoder_1_minutes[6]), .b(sevensegmentdecoder_1_minutes[5]),
    .e(sevensegmentdecoder_1_minutes[2]), .d(sevensegmentdecoder_1_minutes[3]),
    .c(sevensegmentdecoder_1_minutes[4]));  // open: dp
  and_gate and_gate_1 (.a(not_gate_2_o), .b(or_gate_1_rez), .c(and_gate_1_c));
  LED led_17 (.in(and_gate_1_c));

  // Notes on the sheet:
  //   reset
  //   Manual
  //   30
  //   40
  //   60
  //   90
  //   800
  //   1000
  //   1200
  //   Spalare rapida
  //   Camasi
  //   Antialergic
  //   Culori inchise
  //   Rufe murdare
  //   DOOR
  //   prespalare
  //   clatire
  //   clatire
  //   prespalare
  //   1200
  //   1000
  //   800
  //   90
  //   60
  //   40
  //   30
endmodule

module ceva (
  input  [12:0] in_1,
  output [15:0] out_2
);

  time_convert time_convert_1 (.\input (in_1), .\output (out_2));
endmodule

module test (
  input  v0,
  input  v1,
  input  v8,
  input  v7,
  input  v6,
  input  v5,
  input  ok,
  input  rst,
  input  reset,
  input  manual,
  input  t30,
  input  t40,
  input  t60,
  input  [8:0] in_14,
  input  t90,
  input  r800,
  input  in_17,
  input  r1000,
  input  in_19,
  input  r1200,
  input  spalare_rapida,
  input  camasi,
  input  antialergic,
  input  culori_inchise,
  input  rufe_murdare,
  input  door,
  input  prespalare,
  input  in_28,
  output Finn,
  output UsaBlocataa,
  output clatiree,
  output spalaree,
  output prespalaree,
  output evacuaree,
  output incalziree,
  output centrifugaree,
  output Alimentaree,
  output [8:0] out_38,
  output out_39,
  output out_40,
  output out_41
);

  wire alimentare_1_alim, centrifugare_1_centri, clock_1_out, evacuare_1_evac, incalzire_apa_1_fin,
       prewash_1_fin, spalare_principala_1_spalare, undriven;

  Clock clock_1 (.out(clock_1_out));
  alimentare alimentare_1 (.ok(ok), .CLK(clock_1_out), .alim(alimentare_1_alim), .fin(Alimentaree));
  newstarter newstarter_1 (
    .v(in_14), .door(in_17), .start(in_19), .output1(out_39), .output2(out_40), .output3(out_41));  // open: output4, startmasina
  incalzire_apa incalzire_apa_1 (
    .v8(v8), .v7(v7), .v6(v6), .v5(v5), .CLK(clock_1_out), .OK(rst), .fin(incalzire_apa_1_fin),
    .heating(incalziree));
  prewash prewash_1 (.v1(v1), .ok(clock_1_out), .CLK(rst), .prespal(prespalaree), .fin(prewash_1_fin));
  BUTTONmaibun buttonmaibun_1 (
    .reset(reset), .MANUAL(manual), .t30(t30), .t40(t40), .t60(t60), .t90(t90), .r800(r800), .r1000(r1000),
    .r1200(r1200), .SPALARE_RAPIDA(spalare_rapida), .CAMASI(camasi), .ANTIALERGIC(antialergic),
    .CULORI_INCHISE(culori_inchise), .RUFE_MURDARE(rufe_murdare), .DOOR(door), .prespalare(prespalare),
    .clatire(in_28), .v(out_38));
  spalare_principala spalare_principala_1 (
    .ok(prewash_1_fin), .CLK(clock_1_out), .spalare(spalare_principala_1_spalare), .fin(spalaree));
  OR_gate or_gate_1 ();  // open: a, b, c, d, e, f, g, h, rez
  evacuare evacuare_1 (.ok(undriven), .CLK(clock_1_out), .evac(evacuare_1_evac), .fin(evacuaree));
  centrifugare centrifugare_1 (
    .ok(evacuare_1_evac), .CLK(clock_1_out), .centri(centrifugare_1_centri), .fin(centrifugaree));
  usa_blocata usa_blocata_1 (.ok(centrifugare_1_centri), .CLK(clock_1_out), .usa(Finn), .fin(UsaBlocataa));
endmodule

module newdesign (
  input  Input_1,
  input  Input_2,
  input  start,
  input  reset,
  input  manual,
  input  t30,
  input  t40,
  input  t60,
  input  t90,
  input  r800,
  input  r1000,
  input  r1200,
  input  spalare_rapida,
  input  camasi,
  input  antialergic,
  input  culori_inchise,
  input  rufe_murdare,
  input  door,
  input  prespalare,
  input  clatire,
  output [7:0] Output_bus_1,
  output [6:0] Output_bus_2,
  output Output_1,
  output UsaBlocata,
  output Output_2,
  output Output_3,
  output Output_4,
  output Output_5,
  output Output_6,
  output Output_7,
  output Output_8,
  output Output_9
);

  wire frequencydivider_1_clk_1hz, newstarter_1_output1, newstarter_1_startmasina, not_1_out;
  wire [4:0] newstarter_1_output4;
  wire [6:0] buttonmaibun_1_v;
  wire [12:0] counter13_1_q, mux_12to1_1_o;
  wire [15:0] time_convert_1_output;

  FrequencyDivider frequencydivider_1 (.Clock(Input_2), .reset(Input_1), .clk_1hz(frequencydivider_1_clk_1hz));
  BUTTONmaibun buttonmaibun_1 (
    .reset(reset), .MANUAL(manual), .t30(t30), .t40(t40), .t60(t60), .t90(t90), .r800(r800), .r1000(r1000),
    .r1200(r1200), .SPALARE_RAPIDA(spalare_rapida), .CAMASI(camasi), .ANTIALERGIC(antialergic),
    .CULORI_INCHISE(culori_inchise), .RUFE_MURDARE(rufe_murdare), .DOOR(door), .prespalare(prespalare),
    .clatire(clatire), .v({newstarter_1_output4[3], newstarter_1_output4[4], buttonmaibun_1_v}));
  newstarter newstarter_1 (
    .v({newstarter_1_output4[3], newstarter_1_output4[4], buttonmaibun_1_v}), .door(door), .start(start),
    .output1(newstarter_1_output1), .output2(newstarter_1_output4[2]), .output3(newstarter_1_output4[1]),
    .output4(newstarter_1_output4[0]), .startmasina(newstarter_1_startmasina));
  mux_12to1 mux_12to1_1 (.enable(newstarter_1_output1), .sel(newstarter_1_output4), .o(mux_12to1_1_o));
  ProgramMasina ProgramMasina_1 (
    .v1(newstarter_1_output4[4]), .v0(newstarter_1_output4[3]), .v8(buttonmaibun_1_v[0]),
    .v7(buttonmaibun_1_v[1]), .v6(buttonmaibun_1_v[2]), .ok(newstarter_1_startmasina),
    .v5(buttonmaibun_1_v[3]), .clk(frequencydivider_1_clk_1hz), .clatiree(Output_1), .evac(Output_2),
    .heating(Output_3), .prespalare(Output_4), .alim(Output_5), .spalare(Output_6), .centri(Output_7),
    .usa(Output_8), .finalizare(Output_9));
  not not_1 (not_1_out, newstarter_1_startmasina);
  Counter13 counter13_1 (
    .Load(not_1_out), .Clk_EN(newstarter_1_startmasina), .CLK(frequencydivider_1_clk_1hz), .RST(reset),
    .Data(mux_12to1_1_o), .Q(counter13_1_q));
  time_convert time_convert_1 (.\input (counter13_1_q), .\output (time_convert_1_output));
  OR_gate or_gate_1 (
    .a(Output_1), .b(Output_8), .c(Output_2), .d(Output_3), .e(Output_4), .f(Output_5), .g(Output_6),
    .h(Output_7), .rez(UsaBlocata));
  SSD ssd_1 (
    .clk(Input_2), .d0(time_convert_1_output[15:12]), .d1(time_convert_1_output[11:8]),
    .d2(time_convert_1_output[7:4]), .d3(time_convert_1_output[3:0]), .an(Output_bus_1), .cat(Output_bus_2));
endmodule

module afisor (
  input  [12:0] Input_bus_1
);

  wire [15:0] time_convert_1_output;

  time_convert time_convert_1 (.\input (Input_bus_1), .\output (time_convert_1_output));
  SSD ssd_1 ();  // open: clk, d0, d1, d2, d3, an, cat
endmodule

module ProgramMasina (
  input  v1,
  input  v0,
  input  v8,
  input  v7,
  input  v6,
  input  ok,
  input  v5,
  input  clk,
  output clatiree,
  output evac,
  output heating,
  output prespalare,
  output alim,
  output spalare,
  output centri,
  output usa,
  output finalizare
);

  wire alimentare_1_fin, centrifugare_1_fin, clatire_1_fin, evacuare_1_fin, incalzire_apa_1_fin,
       prewash_1_fin, spalare_principala_1_fin;

  alimentare alimentare_1 (.ok(ok), .CLK(clk), .alim(alim), .fin(alimentare_1_fin));
  incalzire_apa incalzire_apa_1 (
    .v8(v8), .v7(v7), .v6(v6), .v5(v5), .CLK(clk), .OK(alimentare_1_fin), .fin(incalzire_apa_1_fin),
    .heating(heating));
  prewash prewash_1 (.v1(v1), .ok(incalzire_apa_1_fin), .CLK(clk), .prespal(prespalare), .fin(prewash_1_fin));
  spalare_principala spalare_principala_1 (
    .ok(prewash_1_fin), .CLK(clk), .spalare(spalare), .fin(spalare_principala_1_fin));
  clatire clatire_1 (.v0(v0), .ok(spalare_principala_1_fin), .CLK(clk), .clat(clatiree), .fin(clatire_1_fin));
  evacuare evacuare_1 (.ok(clatire_1_fin), .CLK(clk), .evac(evac), .fin(evacuare_1_fin));
  centrifugare centrifugare_1 (.ok(evacuare_1_fin), .CLK(clk), .centri(centri), .fin(centrifugare_1_fin));
  usa_blocata usa_blocata_1 (.ok(centrifugare_1_fin), .CLK(clk), .usa(usa), .fin(finalizare));
endmodule

// VHDL entity Counter13, as the project stores it:
LIBRARY ieee;
USE ieee.std_logic_1164.all;

use IEEE.STD_LOGIC_UNSIGNED.ALL;

ENTITY Counter13 IS
  PORT (
		Load, Clk_EN, CLK, RST: in std_logic;
		Data: in std_logic_vector(12 downto 0);
		Q: out std_logic_vector(12 downto 0)
  );
END Counter13;

ARCHITECTURE TypeArchitecture OF Counter13 IS

signal count: std_logic_vector(12 downto 0) := (others => '0');

BEGIN
	
	process (CLK, RST)
	begin
		if RST = '1' then
			count <= (others => '0'); -- Reset the counter to 0
		elsif rising_edge(CLK) then
			if Load = '1' then
				count <= Data;
			else 
				if Clk_EN = '1' then
					count <= count - 1;
				else
					count <= count;
				end if;
			end if;
		end if;
		
		Q <= count;
	end process;

END TypeArchitecture;

// VHDL entity Registru, as the project stores it:
LIBRARY ieee;
USE ieee.std_logic_1164.all;

ENTITY Registru IS
  PORT (load,clk:in std_logic;
  		data:in std_logic_vector (12 downto 0);
  		q:out std_logic_VECTOR (12 downto 0 )

    );
END Registru;

--------------------------------------------------------------------------------
--Complete your VHDL description below
--------------------------------------------------------------------------------

ARCHITECTURE TypeArchitecture OF Registru IS

BEGIN
	process (clk)
	variable reg: std_Logic_vector (12 downto 0) := (others => '0');
	begin
	if rising_edge(clk) then
		if (load ='1') then
			reg:=data;
		else 
			reg:=reg;
		end if;
	end if;
 q<= reg;
 end process;


END TypeArchitecture;

// VHDL entity Adder12Bits, as the project stores it:
LIBRARY ieee;
USE ieee.std_logic_1164.all;
use IEEE.STD_LOGIC_UNSIGNED.ALL;

ENTITY Adder12Bits IS
  PORT (A,B:in std_LOGIC_VECTOR (12 downto 0);
  		rez:out std_logic_vector (12 downto 0)
    );
END Adder12Bits;



ARCHITECTURE TypeArchitecture OF Adder12Bits IS

BEGIN

Rez<=A+B;
END TypeArchitecture;

// VHDL entity BUTTONS, as the project stores it:
LIBRARY ieee;
USE ieee.std_logic_1164.all;

ENTITY BUTTONS IS
  PORT (
   Anulare_prespalare,ANulare_clatire,reset,MANUAL:in STD_LOGIC;
  t30,t40,t60,t90 :in STD_LOGIC;
  r800,r1000,r1200:in STD_LOGIC;
  SPALARE_RAPIDA,CAMASI,ANTIALERGIC,CULORI_INCHISE,RUFE_MURDARE,DOOR:in STD_LOGIC;
  prespalare,clatire :in STD_LOGIC;
  v : out STD_LOGIC_VECTOR(8 downto 0)
    );
END BUTTONS;

ARCHITECTURE TypeArchitecture OF BUTTONS IS

BEGIN
process(reset,t30,t40,t60,t90,r800,r1000,r1200,prespalare,clatire,SPALARE_RAPIDA,CAMASI,ANTIALERGIC,CULORI_INCHISE,RUFE_MURDARE,DOOR,MANUAL,Anulare_Prespalare,Anulare_clatire)
begin
--v(8)=30 v(7) = 40    v(6)=60  v(5) = 90  v(4) =800 v(3) = 1000 v(2) = 1200 presp = v(1) clati = v(0)
if Anulare_prespalare ='1' then v(1) <= '0'; end if;
if Anulare_Clatire ='1' then v(0) <='0'; end if;

if RESET ='1'then --%
v <= "000000000";

elsif DOOR= '1' then--%

   if MANUAL='1' then --&

   if t30 ='1' then v(8) <='1'; 
   elsif t40 ='1' then v(7) <='1';
    elsif t60 ='1' then v(6) <='1'; 
        elsif t90 ='1' then v(5) <='1'; 
          elsif r800 ='1' then v(4) <='1'; 
            elsif r1000 ='1' then v(3) <='1'; 
              elsif r1200 ='1' then v(2) <='1'; 
                 elsif prespalare ='1' then v(1) <='1'; 
                   elsif clatire ='1' then v(0) <='1'; end if;
   else
    if SPALARE_RAPIDA ='1'then --&
v(8) <='1';
    v(2) <='1';
    elsif CAMASI ='1'then
  v(6)<= '1';
    v(4)<= '1';
    elsif CULORI_INCHISE='1'then
     v(0)<='1';
    v(7)<='1';
    v(3) <='1';
    elsif RUFE_MURDARE='1' then
     v(1)<='1';
    v(7)<='1';
    v(3) <='1';
    elsif Antialergic='1' then
    v(0)<='1';
    v(5)<='1';
    v(2)<='1';
   
   end if;--if MANUAL
  end if;
  end if;--%

    end process;

END TypeArchitecture;

// VHDL entity loader, as the project stores it:
LIBRARY ieee;
USE ieee.std_logic_1164.all;

ENTITY loader IS
  PORT (
   reset:in STD_LOGIC;
  t30,t40,t60,t90 :in STD_LOGIC;
  SPALARE_RAPIDA,CAMASI,ANTIALERGIC,CULORI_INCHISE,RUFE_MURDARE,DOOR:in STD_LOGIC;
  v :out STD_LOGIC_VECTOR (12 downto 0)
    );
END loader;


ARCHITECTURE TypeArchitecture OF loader IS

BEGIN
process(reset,t30,t40,t60,t90,SPALARE_RAPIDA,CAMASI,ANTIALERGIC,CULORI_INCHISE,RUFE_MURDARE,DOOR)
begin
if reset ='1' then
 v <= "0000000000000";
 else
   if t30 ='1' and Door ='1' then
    v<= "0100110101011";
    elsif t40 ='1' and Door ='1' then
   v<="0100110111111";
    elsif t60 ='1' and DOOR ='1' then
    v<="0100111100111";
     elsif t90 ='1' and DOOR ='1' then
     v<="0101000100011";
     elsif spalare_rapida='1' and DOOR ='1' then
     v<="0100110101011";
      elsif camasi='1' and DOOR ='1' then
      v<="0100111100111";
       elsif culori_inchise='1' and DOOR ='1' then
       v<="0110000010111";
        elsif rufe_murdare='1' and DOOR ='1' then
        v<="0110000010111";
         elsif antialergic='1' and DOOR ='1' then
          v<="0110001111011";

    end if;
    end if;
    end process;
END TypeArchitecture;

// VHDL entity mux_4to1, as the project stores it:
library ieee;
use ieee.std_logic_1164.all;

entity mux_4to1 is
  port (
    
    sel0, sel1 : in std_logic;
    o : out std_logic_vector(12 downto 0)
  );
end entity mux_4to1;

architecture behavioral of mux_4to1 is

begin

  process(sel0, sel1)
  
  begin
   if sel0 = '0' and sel1 ='0'
   then O <= "0000000000000";
   elsif sel0 ='0' and sel1 = '1'
   then O <= "0001001011000";
   elsif sel0 ='1' and sel1 ='0'
   then O <= "0001001011000";
   elsif sel0 ='1' and sel1 ='1'
   then O<= "0010010110000" ;
   end if;
   
  end process;
end architecture behavioral;

// VHDL entity SevenSegmentDecoder, as the project stores it:
library ieee;
use ieee.std_logic_1164.all;
use ieee.numeric_std.all;

entity SevenSegmentDecoder is
  port (
    Input: in std_logic_vector(15 downto 0);
    
    second,seconds,minute,minutes : out std_logic_vector(6 downto 0)

  );
end entity SevenSegmentDecoder;

architecture Behavioral of SevenSegmentDecoder is
begin

  process(Input)
    variable Value0: integer range 0 to 9;
    variable Value1: integer range 0 to 9;
    variable Value2: integer range 0 to 9;
    variable Value3: integer range 0 to 9;
  begin
    Value0 := to_integer(unsigned(Input(3 downto 0)));
    Value1 := to_integer(unsigned(Input(7 downto 4)));
    Value2 := to_integer(unsigned(Input(11 downto 8)));
    Value3 := to_integer(unsigned(Input(15 downto 12)));
    
    case Value3 is
      when 0 => second <= "1111110";
      when 1 => second <= "0110000";
      when 2 => second <= "1101101";
      when 3 => second <= "1111001";
      when 4 => second <= "0110011";
      
      when 5 => second <= "1011011";
      when 6 => second <= "1011111";
      
      when 7 => second <= "1110000";
      when 8 => second <= "1111111";
      when 9 => second <= "1111011";
      when others => second<= "-------";
    end case;
    
    case Value2 is
      when 0 => seconds <=  "1111110";
      when 1 => seconds <=  "0110000";
      when 2 => seconds <=  "1101101";
      when 3 => seconds <="1111001";
      when 4 => seconds <=  "0110011";
      when 5 => seconds <= "1011011";
      when 6 => seconds <=  "1011111";
      when 7 => seconds <= "1110000";
      when 8 => seconds <=  "1111111";
      when 9 => seconds <=  "1111011";
      when others => seconds <=  "-------";
    end case;

    
    case Value1 is
      when 0 => minute <=  "1111110";
      when 1 => minute <=  "0110000";
      when 2 => minute <=  "1101101";
      when 3 => minute <="1111001";
      when 4 => minute <=  "0110011";
      when 5 => minute <= "1011011";
      when 6 => minute <=  "1011111";
      when 7 => minute <= "1110000";
      when 8 => minute <=  "1111111";
      when 9 => minute <=  "1111011";
      when others => minute <=  "-------";
    end case;

     case Value0 is
      when 0 => minutes <=  "1111110";
      when 1 => minutes <=  "0110000";
      when 2 => minutes <=  "1101101";
      when 3 => minutes <="1111001";
      when 4 => minutes <=  "0110011";
      when 5 => minutes <= "1011011";
      when 6 => minutes <=  "1011111";
      when 7 =>  minutes <= "1110000";
      when 8 => minutes <=  "1111111";
      when 9 => minutes <=  "1111011";
      when others => minutes <=  "-------";
    end case;

   end process;
   end Behavioral;

// VHDL entity time_convert, as the project stores it:
library ieee;
use ieee.std_logic_1164.all;
use ieee.numeric_std.all;

entity time_convert is
  port (
    input : in std_logic_vector(12 downto 0);
    output : out std_logic_vector(15 downto 0)
  );
end time_convert;

architecture TypeArchitecture of time_convert is
  signal minutes : integer range 0 to 70;
  signal seconds : integer range 0 to 59;
  signal num : integer := 0;
--  signal newseconds: integer range 0 to 59;
--  signal newminutes: integer range 0 to 70;

begin

  num <= to_integer(unsigned(input));
  minutes <= num / 60; 
  seconds <= num rem 60;

  process (seconds,minutes,input)
  
  variable temp_seconds: integer := 0;
  variable temp_minutes: integer :=0;
  variable BCD:std_logic_vector(15 downto 0);
  
  begin
  if seconds =0 and minutes =0 then BCD := "0000000000000000" ; 
  else
  if seconds = 0 then
      temp_seconds := 59;
      temp_minutes := minutes -1;
    else 
      temp_seconds := seconds;
      temp_minutes := minutes;
    end if;
  end if;
--newseconds <= temp_seconds;
--newminutes <= temp_minutes;
 BCD (3 downto 0) := std_logic_vector (to_unsigned( temp_seconds rem 10,4));
 BCD (7 downto 4) :=std_logic_vector (to_unsigned( temp_seconds /10 ,4 )); 
 BCD (11 downto 8) := std_logic_vector (to_unsigned( temp_minutes rem 10,4));
 BCD (15 downto 12) :=std_logic_vector (to_unsigned( temp_minutes /10 ,4 ));

 output<=bcd;
  end process;
  
  
end TypeArchitecture;

// VHDL entity starter, as the project stores it:
LIBRARY ieee;
USE ieee.std_logic_1164.all;

ENTITY starter IS
  PORT (
  RESET : in std_logic;
t30,t40,t60,t90 :in STD_LOGIC;
  r800,r1000,r1200:in STD_LOGIC;
  
  START,DOOR :in STD_LOGIC;
  Ok :out std_logic
    );
END starter;



ARCHITECTURE TypeArchitecture OF starter IS
signal okinitial: std_logic := '0';
BEGIN

process (t30,t40,t60,t90,r800,r1000,r1200,DOOR,START )
begin
if RESET ='1' then OKinitial <= '0'; end if;
if DOOR ='1'then
if t30 ='1' or t40='1' or t60 ='1' or t90 ='1'then
if r800 ='1' or r1000 ='1' or r1200 ='1' then
if START ='1' then
OKinitial <= '1';
end if;
end if;
end if;
end if;

ok<=okinitial;
end process;

END TypeArchitecture;

// VHDL entity not_gate, as the project stores it:
-----------------------------------------------

LIBRARY ieee;
USE ieee.std_logic_1164.all;

ENTITY not_gate IS
  PORT (
  i: in std_logic;
  o :out std_logic
    );
END not_gate;


ARCHITECTURE TypeArchitecture OF not_gate IS

BEGIN

o <= not i;
END TypeArchitecture;

// VHDL entity alimentare, as the project stores it:
LIBRARY ieee;
USE ieee.std_logic_1164.all;

use IEEE.STD_LOGIC_UNSIGNED.ALL;

ENTITY alimentare IS
  PORT (
		ok, CLK: in std_logic;
		alim,fin:OUT STD_logic
  );
END alimentare;

ARCHITECTURE TypeArchitecture OF alimentare IS

signal count: std_logic_vector(3 downto 0) := (others => '0');
signal copyalim,copyfin:std_logic:='0';
signal en:std_logic:='1';

BEGIN
	
	process (CLK,ok,en)
	begin
		if ok = '1' and en='1' then
			if rising_edge(CLK) then
				count <= count+1;
				if count="1111" then
					en<='0';
					copyfin<='1';
					copyalim<='0';
				else 
					copyalim<='1';
					copyfin<='0';
				end if;
			end if;
				
		end if;
	end process;
alim<=copyalim;
fin<=copyfin;
END TypeArchitecture;

// VHDL entity incalzire_apa, as the project stores it:
LIBRARY ieee;
USE ieee.std_logic_1164.all;
use IEEE.STD_LOGIC_UNSIGNED.ALL;

ENTITY incalzire_apa IS
  PORT (
    v8, v7, v6, v5, CLK, OK : IN std_logic;
    --q:out std_logic_vector (7 downto 0);
    fin, heating: OUT std_logic
  );
END incalzire_apa;

ARCHITECTURE TypeArchitecture OF incalzire_apa IS
signal count: std_logic_vector(7 downto 0) := (others => '0');
signal en:std_logic:='1';
signal copyfin,copyheating:std_logic:='0';

BEGIN



	process (CLK,en,ok,v8,v7,v6,v5)
	begin

if v8='1' then
count <="00011110";--30
elsif v7='1' then
count <="00101101";--45
elsif v6='1' then
count <="01011010";--90
elsif v5='1' then
count<="10010110";--150
else

		if ok = '1' and en='1' then
			if rising_edge(CLK) then
				count <= count-1;
				if count="00000000" then
					en<='0';
					copyfin<='1';
					copyheating<='0';
				else 
					copyheating<='1';
					copyfin<='0';
				end if;
			end if;
				
		end if;
end if;
	end process;
heating<=copyheating;
fin<=copyfin;
--q<=count;
END TypeArchitecture;

// VHDL entity prewash, as the project stores it:
LIBRARY ieee;
USE ieee.std_logic_1164.all;

use IEEE.STD_LOGIC_UNSIGNED.ALL;

ENTITY prewash IS
  PORT (
		v1,ok, CLK: in std_logic;
		prespal,fin:OUT STD_logic
  );
END prewash;

ARCHITECTURE TypeArchitecture OF prewash IS

signal count: std_logic_vector(9 downto 0) := "0000000000";
signal copyprespal,copyfin:std_logic:='0';
signal en:std_logic:='1';

BEGIN
	
	process (CLK,ok,en,v1)
begin
if v1='1' then
count <="0000001011";
else

		if ok = '1' and en='1' then
			if rising_edge(CLK) then
				count <= count-1;
				if count="0000000000" then
					en<='0';
					copyfin<='1';
					copyprespal<='0';
				else 
					copyprespal<='1';
					copyfin<='0';
				end if;
			end if;
		else 

		end if;
end if;
	end process;
prespal<=copyprespal;
fin<=copyfin;
END TypeArchitecture;

// VHDL entity spalare_principala, as the project stores it:
LIBRARY ieee;
USE ieee.std_logic_1164.all;

use IEEE.STD_LOGIC_UNSIGNED.ALL;

ENTITY spalare_principala IS
  PORT (
		ok, CLK: in std_logic;
		spalare,fin:OUT STD_logic
  );
END spalare_principala;

ARCHITECTURE TypeArchitecture OF spalare_principala IS

signal count: std_logic_vector(10 downto 0) := (others => '0');
signal copyspalare,copyfin:std_logic:='0';
signal en:std_logic:='1';

BEGIN
	
	process (CLK,ok,en)
	begin
		if ok = '1' and en='1' then
			if rising_edge(CLK) then
				count <= count+1;
				if count="00000010001" then
					en<='0';
					copyfin<='1';
					copyspalare<='0';
				else 
					copyspalare<='1';
					copyfin<='0';
				end if;
			end if;
				
		end if;
	end process;
spalare<=copyspalare;
fin<=copyfin;
END TypeArchitecture;

// VHDL entity clatire, as the project stores it:
LIBRARY ieee;
USE ieee.std_logic_1164.all;

use IEEE.STD_LOGIC_UNSIGNED.ALL;

ENTITY clatire IS
  PORT (
		v0,ok, CLK: in std_logic;
		clat,fin:OUT STD_logic
  );
END clatire;

ARCHITECTURE TypeArchitecture OF clatire IS

signal count: std_logic_vector(10 downto 0) := "00000000111";
signal copyclatire,copyfin:std_logic:='0';
signal en:std_logic:='1';

BEGIN
	
	process (CLK,ok,en,v0)
begin
if v0='1' then
count<="00000001111";
else
		if ok = '1' and en='1' then
			if rising_edge(CLK) then
				count <= count-1;
				if count="00000000000" then
					en<='0';
					copyfin<='1';
					copyclatire<='0';
				else 
					copyclatire<='1';
					copyfin<='0';
				end if;
			end if;
				
		end if;
end if;
	end process;
clat<=copyclatire;
fin<=copyfin;
END TypeArchitecture;

// VHDL entity evacuare, as the project stores it:
LIBRARY ieee;
USE ieee.std_logic_1164.all;

use IEEE.STD_LOGIC_UNSIGNED.ALL;

ENTITY evacuare IS
  PORT (
		ok, CLK: in std_logic;
		evac,fin:OUT STD_logic
  );
END evacuare;

ARCHITECTURE TypeArchitecture OF evacuare IS

signal count: std_logic_vector(4 downto 0) := (others => '0');
signal copyevac,copyfin:std_logic:='0';
signal en:std_logic:='1';

BEGIN
	
	process (CLK,ok,en)
	begin
		if ok = '1' and en='1' then
			if rising_edge(CLK) then
				count <= count+1;
				if count="11110" then
					en<='0';
					copyfin<='1';
					copyevac<='0';
				else 
					copyevac<='1';
					copyfin<='0';
				end if;
			end if;
				
		end if;
	end process;
evac<=copyevac;
fin<=copyfin;
END TypeArchitecture;

// VHDL entity centrifugare, as the project stores it:
LIBRARY ieee;
USE ieee.std_logic_1164.all;

use IEEE.STD_LOGIC_UNSIGNED.ALL;

ENTITY centrifugare IS
  PORT (
		ok, CLK: in std_logic;
		centri,fin:OUT STD_logic
  );
END centrifugare;

ARCHITECTURE TypeArchitecture OF centrifugare IS

signal count: std_logic_vector(9 downto 0) := (others => '0');
signal copycentri,copyfin:std_logic:='0';
signal en:std_logic:='1';

BEGIN
	
	process (CLK,ok,en)
	begin
		if ok = '1' and en='1' then
			if rising_edge(CLK) then
				count <= count+1;
				if count="0000001000" then
					en<='0';
					copyfin<='1';
					copycentri<='0';
				else 
					copycentri<='1';
					copyfin<='0';
				end if;
			end if;
				
		end if;
	end process;
centri<=copycentri;
fin<=copyfin;
END TypeArchitecture;

// VHDL entity usa_blocata, as the project stores it:
LIBRARY ieee;
USE ieee.std_logic_1164.all;

use IEEE.STD_LOGIC_UNSIGNED.ALL;

ENTITY usa_blocata IS
  PORT (
		ok, CLK: in std_logic;
		usa,fin:OUT STD_logic
  );
END usa_blocata;

ARCHITECTURE TypeArchitecture OF usa_blocata IS

signal count: std_logic_vector(3 downto 0) := (others => '0');
signal copyusa,copyfin:std_logic:='0';
signal en:std_logic:='1';

BEGIN
	
	process (CLK,ok,en)
	begin
		if ok = '1' and en='1' then
			if rising_edge(CLK) then
				count <= count+1;
				if count="1111" then
					en<='0';
					copyfin<='1';
					copyusa<='0';
				else 
					copyusa<='1';
					copyfin<='0';
				end if;
			end if;
				
		end if;
	end process;
usa<=copyusa;
fin<=copyfin;
END TypeArchitecture;

// VHDL entity OR_gate, as the project stores it:
-------------------------------------------------------------

LIBRARY ieee;
USE ieee.std_logic_1164.all;

ENTITY OR_gate IS
  PORT (
		a,b,c,d,e,f,g,h:in std_logic;
		rez:out std_logic
    );
END OR_gate;


ARCHITECTURE TypeArchitecture OF OR_gate IS

BEGIN

rez <= a or b or c or d or e or f or g or h;

END TypeArchitecture;

// VHDL entity and_gate, as the project stores it:
LIBRARY ieee;
USE ieee.std_logic_1164.all;

ENTITY and_gate IS
  PORT (
 a,b :in std_logic;
 c: out std_logic
    );
END and_gate;


ARCHITECTURE TypeArchitecture OF and_gate IS

BEGIN
c <= a and b;

END TypeArchitecture;

// VHDL entity FrequencyDivider, as the project stores it:
LIBRARY ieee;
USE ieee.std_logic_1164.all;
use ieee.std_logic_unsigned.all;

ENTITY FrequencyDivider IS
  PORT (
Clock: in std_logic;
		reset: in std_logic;
		clk_1hz: out std_logic
    );
END FrequencyDivider;


ARCHITECTURE TypeArchitecture OF FrequencyDivider IS


BEGIN

--64 HZ
process (clock)
	variable  var: std_logic_vector  (25 downto 0) := (others =>'0');
	begin
		if rising_edge (clock) then
			if reset='1' 
				then var:=(others=>'0');
			else
				var:=var+1;
			end if;
		end if;
	clk_1hz <= var(25);
end process;

	
END TypeArchitecture;

// VHDL entity Program, as the project stores it:
LIBRARY ieee;
USE ieee.std_logic_1164.all;

ENTITY Program IS
  PORT (
		v0,v1,v5,v6,v7,v8,rst,ok,clock:in std_logic;
		finn,UsaBlocataa,clatiree,spalaree,prespalaree,evacuaree,incalziree,centrifugaree,alimentaree:out std_Logic
    );
END Program;


-- Main
ARCHITECTURE TypeArchitecture OF Program IS

component alimentare
  PORT (
       Ok,CLK,Reset : in std_logic;
       fin, aliment :out std_logic
    );
END component;
Component incalzire_apa
  PORT (
    v8, v7, v6, v5, CLK, RESET, OK : IN std_logic;
    fin, heating: OUT std_logic
  );
END component;
Component prewash 
  PORT (
    v1,CLK, RESET, OK : IN std_logic;
    prespal, fin: OUT std_logic
    );
END component;
Component spalare_principala
  PORT (
   Ok,CLK,Reset : in std_logic;
       fin, spalare :out std_logic
    );
END component;
Component clatireBoss
  PORT (
    v0,CLK, RESET, OK : IN std_logic;
    clatire, fin: OUT std_logic
    );
END component;
component evacuareBossulica
  PORT (
       Ok,CLK,Reset : in std_logic;
       fin, evacuare :out std_logic
    );
END component;
component centrifugareBoss
  PORT (
       Ok,CLK,Reset : in std_logic;
       fin, centrifugare :out std_logic
    );
END component;
component UsaBlocata
  PORT (
       Ok,CLK,Reset : in std_logic;
       fin, boss :out std_logic
    );
END component;

signal a1,a2,a3,a4,a5,a6,a7: std_logic;
BEGIN

alim: alimentare port map (ok,clock,rst,a1,alimentaree);
incal: incalzire_apa port map (v8,v7,v6,v5,clock,rst,a1,a2,incalziree);
pre: prewash port map (v1,clock,rst,a2,prespalaree,a3);
spal:spalare_principala port map (a3,clock,rst,a4,spalaree);
clat:clatireBoss port map (v0,clock,rst,a4,clatiree,a5);
evac:evacuareBossulica port map (a5,clock,rst,a6,evacuaree);
centr:centrifugareBoss port map (a6,clock,rst,a7,centrifugaree);
usablk:UsaBlocata port map(a7,clock,rst,finn,UsaBlocataa);

END TypeArchitecture;


--alimentare
LIBRARY ieee;
USE ieee.std_logic_1164.all;

ENTITY alimentare IS
  PORT (
       Ok,CLK,Reset : in std_logic;
       fin, aliment :out std_logic
    );
END alimentare;



ARCHITECTURE TypeArchitecture OF alimentare IS
signal en : std_logic := '1';
BEGIN


process(CLK,RESET)
variable count : integer :=15 ;

begin
if RESET ='1' then
en <='1';
count :=15;
fin <='0';
aliment <='0';
end if;
if en ='1' then
if OK ='1' then
aliment <= '1';
fin <='0';
if rising_edge(clk) then
count := count - 1;
else 	
count := count;
		end if;
		end if;	
	if count = 0 then
	fin <= '1';	
	aliment <= '0';
	en <='0';
	end if;
	end if;
	
end process;
END TypeArchitecture;


--incalzire_apa
LIBRARY ieee;
USE ieee.std_logic_1164.all;

ENTITY incalzire_apa IS
  PORT (
    v8, v7, v6, v5, CLK, RESET, OK : IN std_logic;
    fin, heating: OUT std_logic
  );
END incalzire_apa;

ARCHITECTURE TypeArchitecture OF incalzire_apa IS
signal en : std_logic := '1';

BEGIN

process(CLK,RESET)
 VARIABLE count : INTEGER :=0;
    variable copy: integer;
    variable en2: std_logic := '1';
begin

if RESET ='1' then
en <='1';fin <='0';heating <='0';
heating <= '0';
IF v8 = '1' THEN count := 30;en2 := '0'; END IF;
    IF v7 = '1' THEN count := 45;en2 := '0'; END IF;
    IF v6 = '1' THEN count := 90;en2 := '0'; END IF;
    IF v5 = '1' THEN count := 150; en2 := '0';END IF;
end if;

if en2 ='1' then
 IF v8 = '1' THEN count := 30;en2 := '0'; END IF;
    IF v7 = '1' THEN count := 45;en2 := '0'; END IF;
    IF v6 = '1' THEN count := 90;en2 := '0'; END IF;
    IF v5 = '1' THEN count := 150; en2 := '0';END IF;
    
copy := count;

end if;


if en ='1' then
if OK ='1' then  heating <= '1';fin <='0';

if rising_edge(clk) then count := count - 1;
else 	count := count; end if;
				
end if;	
		
	if count = 0 and en2 ='0' then
	fin <= '1';	
	heating <= '0';
	en <='0';
	count :=copy;
	end if;
	end if;
	
end process;
END TypeArchitecture;


--prespalare
LIBRARY ieee;
USE ieee.std_logic_1164.all;

ENTITY prewash IS
  PORT (
    v1,CLK, RESET, OK : IN std_logic;
    prespal, fin: OUT std_logic
    );
END prewash;


ARCHITECTURE TypeArchitecture OF prewash IS
signal en : std_logic := '1';
BEGIN


process(CLK)
variable count : integer :=600 ;

begin

if ok='1' and v1='0' then
fin <= '1';
prespal <='0';
else 
if RESET ='1' then
en <='1';
count :=600;
fin <='0';
prespal <='0';
end if;
if en ='1' then
if OK ='1' then
prespal <= '1';
fin <='0';
if rising_edge(clk) then
count := count - 1;
else 	
count := count;
		end if;
		end if;	
	if count = 0 then
	fin <= '1';	
	prespal<= '0';
	en <='0';
	end if;
	end if;
	
end if;

end process;
END TypeArchitecture;


--spalare_principala
LIBRARY ieee;
USE ieee.std_logic_1164.all;

ENTITY spalare_principala IS
  PORT (
   Ok,CLK,Reset : in std_logic;
       fin, spalare :out std_logic
    );
END spalare_principala;

ARCHITECTURE TypeArchitecture OF spalare_principala IS
signal en : std_logic := '1';
BEGIN


process(CLK,RESET)
variable count : integer :=1200 ;

begin
if RESET ='1' then
en <='1';
count :=1200;
fin <='0';
spalare <='0';
end if;
if en ='1' then
if OK ='1' then
spalare <= '1';
fin <='0';
if rising_edge(clk) then
count := count - 1;
else 	
count := count;
		end if;
		end if;	
	if count = 0 then
	fin <= '1';	
	spalare <= '0';
	en <='0';
	end if;
	end if;
	
end process;
END TypeArchitecture;


--clatire
LIBRARY ieee;
USE ieee.std_logic_1164.all;

ENTITY clatireBoss IS
  PORT (
    v0,CLK, RESET, OK : IN std_logic;
    clatire, fin: OUT std_logic
    );
END clatireBoss;


ARCHITECTURE TypeArchitecture OF clatireboss IS
signal en : std_logic := '1';
signal en2: std_logic := '1';
BEGIN


process(CLK)
variable count : integer :=10 ;

begin

if ok='1' and v0='1' and en2= '1' then
count := 1200;
en2 <= '0';
elsif ok='1' and v0='0'and en2= '1' then
		count :=600;
		en2 <= '0';
else
if RESET ='1' then
en <='1';
count :=10;
en2 <= '1';
fin <='0';
clatire <='0';
end if;
if en ='1' then
if OK ='1' then
clatire <= '1';
fin <='0';
if rising_edge(clk) then
count := count - 1;
else 	
count := count;
		end if;
		end if;	
	if count = 0 then
	fin <= '1';	
	clatire<= '0';
	en <='0';
	end if;
	
end if;
end if;

end process;
END TypeArchitecture;


--evacuare
LIBRARY ieee;
USE ieee.std_logic_1164.all;

ENTITY evacuareBossulica IS
  PORT (
       Ok,CLK,Reset : in std_logic;
       fin, evacuare :out std_logic
    );
END evacuareBossulica;



ARCHITECTURE TypeArchitecture OF evacuareBossulica IS
signal en : std_logic := '1';
BEGIN


process(CLK,RESET)
variable count : integer :=30 ;

begin
if RESET ='1' then
en <='1';
count :=30;
fin <='0';
evacuare<='0';
end if;
if en ='1' then
if OK ='1' then
evacuare <= '1';
fin <='0';
if rising_edge(clk) then
count := count - 1;
else 	
count := count;
		end if;
		end if;	
	if count = 0 then
	fin <= '1';	
	evacuare <= '0';
	en <='0';
	end if;
	end if;
	
end process;
END TypeArchitecture;


--centrifugare
LIBRARY ieee;
USE ieee.std_logic_1164.all;

ENTITY centrifugareBoss IS
  PORT (
       Ok,CLK,Reset : in std_logic;
       fin, centrifugare :out std_logic
    );
END centrifugareBoss;



ARCHITECTURE TypeArchitecture OF centrifugareBoss IS
signal en : std_logic := '1';
BEGIN


process(CLK,RESET)
variable count : integer :=600 ;

begin
if RESET ='1' then
en <='1';
count :=600;
fin <='0';
centrifugare <='0';
end if;
if en ='1' then
if OK ='1' then
Centrifugare <= '1';
fin <='0';
if rising_edge(clk) then
count := count - 1;
else 	
count := count;
		end if;
		end if;	
	if count = 0 then
	fin <= '1';	
	centrifugare <= '0';
	en <='0';
	end if;
	end if;
	
end process;
END TypeArchitecture;


--usa_blocata
LIBRARY ieee;
USE ieee.std_logic_1164.all;

ENTITY UsaBlocata IS
  PORT (
       Ok,CLK,Reset : in std_logic;
       fin, boss :out std_logic
    );
END UsaBlocata;

ARCHITECTURE TypeArchitecture OF UsaBlocata IS
signal en : std_logic := '1';
BEGIN


process(CLK,RESET)
variable count : integer :=60 ;

begin
if RESET ='1' then
en <='1';
count :=60;
fin <='0';
boss<='0';
end if;
if en ='1' then
if OK ='1' then
boss <= '1';
fin <='0';
if rising_edge(clk) then
count := count - 1;
else 	
count := count;
		end if;
		end if;	
	if count = 0 then
	fin <= '1';	
	boss <= '0';
	en <='0';
	end if;
	end if;
	
end process;

END TypeArchitecture;

// VHDL entity MasinaDeSpalat, as the project stores it:
-- Main
LIBRARY ieee;
USE ieee.std_logic_1164.all;

ENTITY MasinaDeSpalat IS
  PORT (anulare_prespalare,anulare_clatire,reset,Manual:in std_logic ;
		t30,t40,t60,t90,r800,r1000,r1200:in std_logic;
		spalare_rapida,camasi,antialergic,culori_inchise,rufe_murdare,Door,prespalare,clatire:in std_logic;
		start,clock:in std_logic;
		--20 inputs

		--loadregister:in std_logic;
		-- for register

		clatireOut,prespalareOut,r1200out,r1000out,r800out,t90out,t60out,t40out,t30out:out std_logic;
		--outputs from buttons

		clatiree,spalaree,prespalaree,evacuaree,incalziree,centrifugaree,alimentaree:out std_Logic;
		--outputs from program

		second,seconds,minute,minutes:out std_logic_vector(6 downto 0);
		--for 7 segment display

		ledusablocata:out std_logic
    );
END MasinaDeSpalat;



ARCHITECTURE TypeArchitecture OF MasinaDeSpalat IS

-- Component declaration
------------------------------------------------------------------------------------------------------------
component BUTTONS
  PORT (
   Anulare_prespalare,ANulare_clatire,reset,MANUAL:in STD_LOGIC;
  t30,t40,t60,t90 :in STD_LOGIC;
  r800,r1000,r1200:in STD_LOGIC;
  SPALARE_RAPIDA,CAMASI,ANTIALERGIC,CULORI_INCHISE,RUFE_MURDARE,DOOR:in STD_LOGIC;
  prespalare,clatire :in STD_LOGIC;
  v : out STD_LOGIC_VECTOR(8 downto 0)
    );
END component;

component Registru 
  PORT (
load,clk:in std_logic;
  		data:in std_logic_vector (12 downto 0);
  		q:out std_logic_VECTOR (12 downto 0 )

    );
END component;

Component loader
  PORT (
   reset:in STD_LOGIC;
  t30,t40,t60,t90 :in STD_LOGIC;
  SPALARE_RAPIDA,CAMASI,ANTIALERGIC,CULORI_INCHISE,RUFE_MURDARE,DOOR:in STD_LOGIC;
  v :out STD_LOGIC_VECTOR (12 downto 0)
    );
END component;

Component mux_4to1 
  port (
    
    sel0, sel1 : in std_logic;
    o : out std_logic_vector(12 downto 0)
  );
end component;

Component Adder12Bits
  PORT (
A,B:in std_LOGIC_VECTOR (12 downto 0);
  		rez:out std_logic_vector (12 downto 0)
    );
END component;

component Counter13
  PORT (
		Load, Clk_EN, CLK, RST: in std_logic;
		Data: in std_logic_vector(12 downto 0);
		Q: out std_logic_vector(12 downto 0)
  );
END component;

component time_convert
  port (
    input : in std_logic_vector(12 downto 0);
    output : out std_logic_vector(15 downto 0)
  );
end component;

component SevenSegmentDecoder
  port (
    Input: in std_logic_vector(15 downto 0);
    
    second,seconds,minute,minutes : out std_logic_vector(6 downto 0)

  );
end component;

component Program
  PORT (
		v0,v1,v5,v6,v7,v8,rst,ok,clock:in std_logic;
		finn,UsaBlocataa,clatiree,spalaree,prespalaree,evacuaree,incalziree,centrifugaree,alimentaree:out std_Logic
    );
END component;

component starter
  PORT (
  RESET : in std_logic;
t30,t40,t60,t90 :in STD_LOGIC;
  r800,r1000,r1200:in STD_LOGIC;
  
  START,DOOR :in STD_LOGIC;
  Ok :out std_logic
    );
END component;

component not_gate
  PORT (
  i: in std_logic;
  o :out std_logic
    );
END component;

component OR_gate
  PORT (
		a,b:in std_logic;
		rez:out std_logic
    );
END component ;

component and_gate
  PORT (
 a,b :in std_logic;
 c: out std_logic
    );
END component;

component FrequencyDivider
  PORT (
Clock: in std_logic;
		reset: in std_logic;
		clk_1hz: out std_logic
    );
END component;

-- signals declarations
--------------------------------------------------------------------------------------

signal vbuttons: std_Logic_vector (8 downto 0);
signal vloader: std_Logic_vector (12 downto 0);
signal qregister: std_logic_vector(12 downto 0);
signal omux:std_Logic_vector (12 downto 0 );
signal rezadder: std_logic_vector(12 downto 0);
signal qcounter:std_logic_vector(12 downto 0);
signal outtimeconverter:std_logic_vector(15 downto 0);
signal okstarter:std_logic;
signal programfinn,usablok:std_logic;
signal outnot1,outnot2,outor:std_logic;
signal freqdiv1,freqdiv2:std_logic;
constant VCC : std_logic := '1';

BEGIN

but: Buttons port map (Anulare_prespalare,ANulare_clatire,reset,MANUAL,t30,t40,t60,t90,r800,r1000,r1200,SPALARE_RAPIDA,CAMASI,ANTIALERGIC,CULORI_INCHISE,RUFE_MURDARE,DOOR,prespalare,clatire ,vbuttons);
load: loader port map ( reset, t30,t40,t60,t90,SPALARE_RAPIDA,CAMASI,ANTIALERGIC,CULORI_INCHISE,RUFE_MURDARE,DOOR,vloader);
reg: registru port map (VCC,clock,vloader,qregister);
mux:mux_4to1 port map(vbuttons(1),vbuttons(2),omux);
Add: adder12bits port map (omux,qregister,rezadder);
not1:not_gate port map (okstarter,outnot1);
--freq1:FrequencyDivider port map (clock,reset,freqdiv1);
count: counter13 port map (outnot1,okstarter,clock,reset,rezadder,qcounter);
timeconv:time_convert port map (qcounter,outtimeconverter);
sevenseg:SevenSegmentDecoder port map (outtimeconverter,second,seconds,minute,minutes);
starterrr:starter port map (reset,vbuttons(8),vbuttons(7),vbuttons(6),vbuttons(5),vbuttons(4),vbuttons(3),vbuttons(2),start,door,okstarter);
--freq2: FrequencyDivider port map (clock,reset,freqdiv2);
progamul:program port map (vbuttons(0),vbuttons(1),vbuttons(5),vbuttons(6),vbuttons(7),vbuttons(8),reset,okstarter,clock,programfinn,usablok,clatiree,spalaree,prespalaree,evacuaree,incalziree,centrifugaree,alimentaree);
not2:not_gate port map (programfinn,outnot2);
orgate: or_gate port map (usablok,okstarter,outor);
andgate:and_gate port map (outnot2,outor,ledusablocata);

END TypeArchitecture;



-- Buttons


LIBRARY ieee;
USE ieee.std_logic_1164.all;

ENTITY BUTTONS IS
  PORT (
   Anulare_prespalare,ANulare_clatire,reset,MANUAL:in STD_LOGIC;
  t30,t40,t60,t90 :in STD_LOGIC;
  r800,r1000,r1200:in STD_LOGIC;
  SPALARE_RAPIDA,CAMASI,ANTIALERGIC,CULORI_INCHISE,RUFE_MURDARE,DOOR:in STD_LOGIC;
  prespalare,clatire :in STD_LOGIC;
  v : out STD_LOGIC_VECTOR(8 downto 0)
    );
END BUTTONS;

ARCHITECTURE TypeArchitecture OF BUTTONS IS

BEGIN
process(reset,t30,t40,t60,t90,r800,r1000,r1200,prespalare,clatire,SPALARE_RAPIDA,CAMASI,ANTIALERGIC,CULORI_INCHISE,RUFE_MURDARE,DOOR,MANUAL,Anulare_Prespalare,Anulare_clatire)
begin
--v(8)=30 v(7) = 40    v(6)=60  v(5) = 90  v(4) =800 v(3) = 1000 v(2) = 1200 presp = v(1) clati = v(0)
if Anulare_prespalare ='1' then v(1) <= '0'; end if;
if Anulare_Clatire ='1' then v(0) <='0'; end if;

if RESET ='1'then --%
v <= "000000000";

elsif DOOR= '1' then--%

   if MANUAL='1' then --&

   if t30 ='1' then v(8) <='1'; end if;
     if t40 ='1' then v(7) <='1'; end if;
       if t60 ='1' then v(6) <='1'; end if;
         if t90 ='1' then v(5) <='1'; end if;
           if r800 ='1' then v(4) <='1'; end if;
             if r1000 ='1' then v(3) <='1'; end if;
               if r1200 ='1' then v(2) <='1'; end if;
                 if prespalare ='1' then v(1) <='1'; end if;
                   if clatire ='1' then v(0) <='1'; end if;
   else
    if SPALARE_RAPIDA ='1'then --&
v(8) <='1';
    v(2) <='1';
    elsif CAMASI ='1'then
  v(6)<= '1';
    v(4)<= '1';
    elsif CULORI_INCHISE='1'then
     v(0)<='1';
    v(7)<='1';
    v(3) <='1';
    elsif RUFE_MURDARE='1' then
     v(1)<='1';
    v(7)<='1';
    v(3) <='1';
    elsif Antialergic='1' then
    v(0)<='1';
    v(5)<='1';
    v(2)<='1';
   
   end if;--if MANUAL
  end if;

  end if;--%

    end process;
    
END TypeArchitecture;



-- Register


LIBRARY ieee;
USE ieee.std_logic_1164.all;

ENTITY Registru IS
  PORT (
load,clk:in std_logic;
  		data:in std_logic_vector (12 downto 0);
  		q:out std_logic_VECTOR (12 downto 0 )

    );
END Registru;


ARCHITECTURE TypeArchitecture OF Registru IS

BEGIN

	process (clk)
	variable reg: std_Logic_vector (12 downto 0) := (others => '0');
	begin
	if rising_edge(clk) then
		if (load ='1') then
			reg:=data;
		else 
			reg:=reg;
		end if;
	end if;
 q<= reg;
 end process;


END TypeArchitecture;



-- Loader


LIBRARY ieee;
USE ieee.std_logic_1164.all;

ENTITY loader IS
  PORT (
   reset:in STD_LOGIC;
  t30,t40,t60,t90 :in STD_LOGIC;
  SPALARE_RAPIDA,CAMASI,ANTIALERGIC,CULORI_INCHISE,RUFE_MURDARE,DOOR:in STD_LOGIC;
  v :out STD_LOGIC_VECTOR (12 downto 0)
    );
END loader;


ARCHITECTURE TypeArchitecture OF loader IS

BEGIN
process(reset,t30,t40,t60,t90,SPALARE_RAPIDA,CAMASI,ANTIALERGIC,CULORI_INCHISE,RUFE_MURDARE,DOOR)
begin
if reset ='1' then
 v <= "0000000000000";
 else
   if t30 ='1' and Door ='1' then
    v<= "0100110101011";
    elsif t40 ='1' and Door ='1' then

   v<="0100110111111";
    elsif t60 ='1' and DOOR ='1' then
    v<="0100111100111";
     elsif t90 ='1' and DOOR ='1' then
     v<="0101000100011";
     elsif spalare_rapida='1' and DOOR ='1' then
     v<="0100110101011";
      elsif camasi='1' and DOOR ='1' then
      v<="0100111100111";
       elsif culori_inchise='1' and DOOR ='1' then
       v<="0110000010111";
        elsif rufe_murdare='1' and DOOR ='1' then
        v<="0110000010111";
         elsif antialergic='1' and DOOR ='1' then

          v<="0110001111011";

    end if;
    end if;
    end process;
END TypeArchitecture;



-- mux 4:1


library ieee;
use ieee.std_logic_1164.all;

entity mux_4to1 is
  port (
    
    sel0, sel1 : in std_logic;
    o : out std_logic_vector(12 downto 0)
  );
end entity mux_4to1;

architecture behavioral of mux_4to1 is

begin

  process(sel0, sel1)
  
  begin
   if sel0 = '0' and sel1 ='0'
   then O <= "0000000000000";
   elsif sel0 ='0' and sel1 = '1'
   then O <= "0001001011000";
   elsif sel0 ='1' and sel1 ='0'
   then O <= "0001001011000";
   elsif sel0 ='1' and sel1 ='1'
   then O<= "0010010110000" ;
   end if;
   
  end process;
end architecture behavioral;



-- Adder


LIBRARY ieee;
USE ieee.std_logic_1164.all;
use IEEE.STD_LOGIC_UNSIGNED.ALL;

ENTITY Adder12Bits IS
  PORT (
A,B:in std_LOGIC_VECTOR (12 downto 0);
  		rez:out std_logic_vector (12 downto 0)
    );
END Adder12Bits;



ARCHITECTURE TypeArchitecture OF Adder12Bits IS

BEGIN


Rez<=A+B;
END TypeArchitecture;



-- Counter 


LIBRARY ieee;
USE ieee.std_logic_1164.all;

use IEEE.STD_LOGIC_UNSIGNED.ALL;

ENTITY Counter13 IS
  PORT (
		Load, Clk_EN, CLK, RST: in std_logic;
		Data: in std_logic_vector(12 downto 0);
		Q: out std_logic_vector(12 downto 0)
  );
END Counter13;

ARCHITECTURE TypeArchitecture OF Counter13 IS

signal count: std_logic_vector(12 downto 0) := (others => '0');

BEGIN
	
	process (CLK, RST)
	begin
		if RST = '1' then
			count <= (others => '0'); -- Reset the counter to 0
		elsif rising_edge(CLK) then
			if Load = '1' then
				count <= Data;
			else 
				if Clk_EN = '1' then
					count <= count - 1;
				else
					count <= count;
				end if;
			end if;
		end if;
		
		Q <= count;
	end process;

END TypeArchitecture;



-- time converter


library ieee;
use ieee.std_logic_1164.all;
use ieee.numeric_std.all;

entity time_convert is
  port (
    input : in std_logic_vector(12 downto 0);
    output : out std_logic_vector(15 downto 0)
  );
end time_convert;

architecture TypeArchitecture of time_convert is
  signal minutes : integer range 0 to 70;
  signal seconds : integer range 0 to 59;
  signal num : integer := 0;
--  signal newseconds: integer range 0 to 59;
--  signal newminutes: integer range 0 to 70;

begin

  num <= to_integer(unsigned(input));
  minutes <= num / 60; 
  seconds <= num rem 60;

  process (seconds,minutes,input)
  
  variable temp_seconds: integer := 0;
  variable temp_minutes: integer :=0;
  variable BCD:std_logic_vector(15 downto 0);
  
  begin
  if seconds =0 and minutes =0 then output <= "0000000000000000" ; 
  else
  if seconds = 0 then
      temp_seconds := 59;
      temp_minutes := minutes -1;
    else 
      temp_seconds := seconds;
      temp_minutes := minutes;
    end if;
  end if;
--newseconds <= temp_seconds;
--newminutes <= temp_minutes;
 BCD (3 downto 0) := std_logic_vector (to_unsigned( temp_seconds rem 10,4));
 BCD (7 downto 4) :=std_logic_vector (to_unsigned( temp_seconds /10 ,4 )); 
 BCD (11 downto 8) := std_logic_vector (to_unsigned( temp_minutes rem 10,4));
 BCD (15 downto 12) :=std_logic_vector (to_unsigned( temp_minutes /10 ,4 ));

 output<=bcd;
  end process;
  
  
end TypeArchitecture;



-- Seven Segment Decoder


library ieee;
use ieee.std_logic_1164.all;
use ieee.numeric_std.all;

entity SevenSegmentDecoder is
  port (
    Input: in std_logic_vector(15 downto 0);
    
    second,seconds,minute,minutes : out std_logic_vector(6 downto 0)

  );
end entity SevenSegmentDecoder;

architecture Behavioral of SevenSegmentDecoder is
begin

  process(Input)
    variable Value0: integer range 0 to 9;
    variable Value1: integer range 0 to 9;
    variable Value2: integer range 0 to 9;
    variable Value3: integer range 0 to 9;
  begin
    Value0 := to_integer(unsigned(Input(3 downto 0)));
    Value1 := to_integer(unsigned(Input(7 downto 4)));
    Value2 := to_integer(unsigned(Input(11 downto 8)));
    Value3 := to_integer(unsigned(Input(15 downto 12)));
    
    case Value3 is
      when 0 => second <= "1111110";
      when 1 => second <= "0110000";
      when 2 => second <= "1101101";
      when 3 => second <= "1111001";
      when 4 => second <= "0110011";
      
      when 5 => second <= "1011011";
      when 6 => second <= "1011111";
      
      when 7 => second <= "1110000";
      when 8 => second <= "1111111";
      when 9 => second <= "1111011";
      when others => second<= "-------";
    end case;
    
    case Value2 is
      when 0 => seconds <=  "1111110";
      when 1 => seconds <=  "0110000";
      when 2 => seconds <=  "1101101";
      when 3 => seconds <="1111001";
      when 4 => seconds <=  "0110011";
      when 5 => seconds <= "1011011";
      when 6 => seconds <=  "1011111";
      when 7 => seconds <= "1110000";
      when 8 => seconds <=  "1111111";
      when 9 => seconds <=  "1111011";
      when others => seconds <=  "-------";
    end case;

    
    case Value1 is
      when 0 => minute <=  "1111110";
      when 1 => minute <=  "0110000";
      when 2 => minute <=  "1101101";
      when 3 => minute <="1111001";
      when 4 => minute <=  "0110011";
      when 5 => minute <= "1011011";
      when 6 => minute <=  "1011111";
      when 7 => minute <= "1110000";
      when 8 => minute <=  "1111111";
      when 9 => minute <=  "1111011";
      when others => minute <=  "-------";
    end case;

     case Value0 is
      when 0 => minutes <=  "1111110";
      when 1 => minutes <=  "0110000";
      when 2 => minutes <=  "1101101";
      when 3 => minutes <="1111001";
      when 4 => minutes <=  "0110011";
      when 5 => minutes <= "1011011";
      when 6 => minutes <=  "1011111";
      when 7 =>  minutes <= "1110000";
      when 8 => minutes <=  "1111111";
      when 9 => minutes <=  "1111011";
      when others => minutes <=  "-------";
    end case;

   end process;
   end Behavioral;



-- Program


LIBRARY ieee;
USE ieee.std_logic_1164.all;

ENTITY Program IS
  PORT (
		v0,v1,v5,v6,v7,v8,rst,ok,clock:in std_logic;
		finn,UsaBlocataa,clatiree,spalaree,prespalaree,evacuaree,incalziree,centrifugaree,alimentaree:out std_Logic
    );
END Program;



-- Main Program
ARCHITECTURE TypeArchitecture OF Program IS

component alimentare
  PORT (
       Ok,CLK,Reset : in std_logic;
       fin, aliment :out std_logic
    );
END component;
Component incalzire_apa
  PORT (
    v8, v7, v6, v5, CLK, RESET, OK : IN std_logic;
    fin, heating: OUT std_logic
  );
END component;
Component prewash 
  PORT (
    v1,CLK, RESET, OK : IN std_logic;
    prespal, fin: OUT std_logic
    );
END component;
Component spalare_principala
  PORT (
   Ok,CLK,Reset : in std_logic;
       fin, spalare :out std_logic
    );
END component;
Component clatireBoss
  PORT (
    v0,CLK, RESET, OK : IN std_logic;
    clatire, fin: OUT std_logic
    );
END component;
component evacuareBossulica
  PORT (
       Ok,CLK,Reset : in std_logic;
       fin, evacuare :out std_logic
    );
END component;
component centrifugareBoss
  PORT (
       Ok,CLK,Reset : in std_logic;
       fin, centrifugare :out std_logic
    );
END component;
component UsaBlocata
  PORT (
       Ok,CLK,Reset : in std_logic;
       fin, boss :out std_logic
    );
END component;

signal a1,a2,a3,a4,a5,a6,a7: std_logic;
BEGIN


alim: alimentare port map (ok,clock,rst,a1,alimentaree);
incal: incalzire_apa port map (v8,v7,v6,v5,clock,rst,a1,a2,incalziree);

pre: prewash port map (v1,clock,rst,a2,prespalaree,a3);
spal:spalare_principala port map (a3,clock,rst,a4,spalaree);
clat:clatireBoss port map (v0,clock,rst,a4,clatiree,a5);
evac:evacuareBossulica port map (a5,clock,rst,a6,evacuaree);
centr:centrifugareBoss port map (a6,clock,rst,a7,centrifugaree);
usablk:UsaBlocata port map(a7,clock,rst,finn,UsaBlocataa);

END TypeArchitecture;


-- alimentare
LIBRARY ieee;
USE ieee.std_logic_1164.all;

ENTITY alimentare IS
  PORT (
       Ok,CLK,Reset : in std_logic;
       fin, aliment :out std_logic
    );
END alimentare;



ARCHITECTURE TypeArchitecture OF alimentare IS
signal en : std_logic := '1';
BEGIN


process(CLK,RESET)
variable count : integer :=15 ;

begin
if RESET ='1' then
en <='1';
count :=15;
fin <='0';
aliment <='0';
end if;
if en ='1' then
if OK ='1' then
aliment <= '1';
fin <='0';
if rising_edge(clk) then
count := count - 1;
else 	
count := count;
		end if;
		end if;	
	if count = 0 then
	fin <= '1';	
	aliment <= '0';
	en <='0';
	end if;
	end if;
	
end process;
END TypeArchitecture;


-- incalzire_apa
LIBRARY ieee;
USE ieee.std_logic_1164.all;

ENTITY incalzire_apa IS
  PORT (
    v8, v7, v6, v5, CLK, RESET, OK : IN std_logic;
    fin, heating: OUT std_logic
  );
END incalzire_apa;

ARCHITECTURE TypeArchitecture OF incalzire_apa IS
signal en : std_logic := '1';

BEGIN

process(CLK,RESET)
 VARIABLE count : INTEGER :=0;
    variable copy: integer;
    variable en2: std_logic := '1';
begin

if RESET ='1' then
en <='1';fin <='0';heating <='0';
heating <= '0';
IF v8 = '1' THEN count := 30;en2 := '0'; END IF;
    IF v7 = '1' THEN count := 45;en2 := '0'; END IF;
    IF v6 = '1' THEN count := 90;en2 := '0'; END IF;
    IF v5 = '1' THEN count := 150; en2 := '0';END IF;
end if;

if en2 ='1' then
 IF v8 = '1' THEN count := 30;en2 := '0'; END IF;
    IF v7 = '1' THEN count := 45;en2 := '0'; END IF;
    IF v6 = '1' THEN count := 90;en2 := '0'; END IF;
    IF v5 = '1' THEN count := 150; en2 := '0';END IF;
    
copy := count;

end if;


if en ='1' then
if OK ='1' then  heating <= '1';fin <='0';

if rising_edge(clk) then count := count - 1;
else 	count := count; end if;
				
end if;	
		
	if count = 0 and en2 ='0' then
	fin <= '1';	
	heating <= '0';
	en <='0';
	count :=copy;
	end if;
	end if;
	
end process;
END TypeArchitecture;


-- prespalare
LIBRARY ieee;
USE ieee.std_logic_1164.all;

ENTITY prewash IS
  PORT (
    v1,CLK, RESET, OK : IN std_logic;
    prespal, fin: OUT std_logic
    );
END prewash;


ARCHITECTURE TypeArchitecture OF prewash IS
signal en : std_logic := '1';
BEGIN


process(CLK)
variable count : integer :=600 ;

begin

if ok='1' and v1='0' then
fin <= '1';
prespal <='0';
else 
if RESET ='1' then
en <='1';
count :=600;
fin <='0';
prespal <='0';
end if;
if en ='1' then
if OK ='1' then
prespal <= '1';
fin <='0';
if rising_edge(clk) then
count := count - 1;
else 	
count := count;
		end if;
		end if;	
	if count = 0 then
	fin <= '1';	
	prespal<= '0';
	en <='0';
	end if;
	end if;
	
end if;

end process;
END TypeArchitecture;


-- spalare_principala
LIBRARY ieee;
USE ieee.std_logic_1164.all;

ENTITY spalare_principala IS
  PORT (
   Ok,CLK,Reset : in std_logic;
       fin, spalare :out std_logic
    );
END spalare_principala;

ARCHITECTURE TypeArchitecture OF spalare_principala IS
signal en : std_logic := '1';
BEGIN


process(CLK,RESET)
variable count : integer :=1200 ;

begin
if RESET ='1' then
en <='1';
count :=1200;
fin <='0';
spalare <='0';
end if;
if en ='1' then
if OK ='1' then
spalare <= '1';
fin <='0';
if rising_edge(clk) then
count := count - 1;
else 	
count := count;
		end if;
		end if;	
	if count = 0 then
	fin <= '1';	
	spalare <= '0';
	en <='0';
	end if;
	end if;
	
end process;
END TypeArchitecture;


-- clatire
LIBRARY ieee;
USE ieee.std_logic_1164.all;

ENTITY clatireBoss IS
  PORT (
    v0,CLK, RESET, OK : IN std_logic;
    clatire, fin: OUT std_logic
    );
END clatireBoss;


ARCHITECTURE TypeArchitecture OF clatireboss IS
signal en : std_logic := '1';
signal en2: std_logic := '1';
BEGIN


process(CLK)
variable count : integer :=10 ;

begin

if ok='1' and v0='1' and en2= '1' then
count := 1200;
en2 <= '0';
elsif ok='1' and v0='0'and en2= '1' then
		count :=600;
		en2 <= '0';
else
if RESET ='1' then
en <='1';
count :=10;
en2 <= '1';
fin <='0';
clatire <='0';
end if;
if en ='1' then
if OK ='1' then
clatire <= '1';
fin <='0';
if rising_edge(clk) then
count := count - 1;
else 	
count := count;
		end if;
		end if;	
	if count = 0 then
	fin <= '1';	
	clatire<= '0';
	en <='0';
	end if;
	
end if;
end if;

end process;
END TypeArchitecture;


-- evacuare
LIBRARY ieee;
USE ieee.std_logic_1164.all;

ENTITY evacuareBossulica IS
  PORT (
       Ok,CLK,Reset : in std_logic;
       fin, evacuare :out std_logic
    );
END evacuareBossulica;



ARCHITECTURE TypeArchitecture OF evacuareBossulica IS
signal en : std_logic := '1';
BEGIN


process(CLK,RESET)
variable count : integer :=30 ;

begin
if RESET ='1' then
en <='1';
count :=30;
fin <='0';
evacuare<='0';
end if;
if en ='1' then
if OK ='1' then
evacuare <= '1';
fin <='0';
if rising_edge(clk) then
count := count - 1;
else 	
count := count;
		end if;
		end if;	
	if count = 0 then
	fin <= '1';	
	evacuare <= '0';
	en <='0';
	end if;
	end if;
	
end process;
END TypeArchitecture;


-- centrifugare
LIBRARY ieee;
USE ieee.std_logic_1164.all;

ENTITY centrifugareBoss IS
  PORT (
       Ok,CLK,Reset : in std_logic;
       fin, centrifugare :out std_logic
    );
END centrifugareBoss;



ARCHITECTURE TypeArchitecture OF centrifugareBoss IS
signal en : std_logic := '1';
BEGIN


process(CLK,RESET)
variable count : integer :=600 ;

begin
if RESET ='1' then
en <='1';
count :=600;
fin <='0';
centrifugare <='0';
end if;
if en ='1' then
if OK ='1' then
Centrifugare <= '1';
fin <='0';
if rising_edge(clk) then
count := count - 1;
else 	
count := count;
		end if;
		end if;	
	if count = 0 then
	fin <= '1';	
	centrifugare <= '0';
	en <='0';
	end if;
	end if;
	
end process;
END TypeArchitecture;


-- usa_blocata
LIBRARY ieee;
USE ieee.std_logic_1164.all;

ENTITY UsaBlocata IS
  PORT (
       Ok,CLK,Reset : in std_logic;
       fin, boss :out std_logic
    );
END UsaBlocata;

ARCHITECTURE TypeArchitecture OF UsaBlocata IS
signal en : std_logic := '1';
BEGIN


process(CLK,RESET)
variable count : integer :=60 ;

begin
if RESET ='1' then
en <='1';
count :=60;
fin <='0';
boss<='0';
end if;
if en ='1' then
if OK ='1' then
boss <= '1';
fin <='0';
if rising_edge(clk) then
count := count - 1;
else 	
count := count;
		end if;
		end if;	
	if count = 0 then
	fin <= '1';	
	boss <= '0';
	en <='0';
	end if;
	end if;
	
end process;

END TypeArchitecture;



-- starter


LIBRARY ieee;
USE ieee.std_logic_1164.all;

ENTITY starter IS
  PORT (
  RESET : in std_logic;
t30,t40,t60,t90 :in STD_LOGIC;
  r800,r1000,r1200:in STD_LOGIC;
  
  START,DOOR :in STD_LOGIC;
  Ok :out std_logic
    );
END starter;



ARCHITECTURE TypeArchitecture OF starter IS

BEGIN


process (t30,t40,t60,t90,r800,r1000,r1200,DOOR,START )
begin
if RESET ='1' then OK <= '0'; end if;
if DOOR ='1'then
if t30 ='1' or t40='1' or t60 ='1' or t90 ='1'then
if r800 ='1' or r1000 ='1' or r1200 ='1' then
if START ='1' then
OK <= '1';
end if;
end if;
end if;
end if;


end process;

END TypeArchitecture;



-- not gate


LIBRARY ieee;
USE ieee.std_logic_1164.all;

ENTITY not_gate IS
  PORT (
  i: in std_logic;
  o :out std_logic
    );
END not_gate;


ARCHITECTURE TypeArchitecture OF not_gate IS

BEGIN

o <= not i;
END TypeArchitecture;



-- or gate


LIBRARY ieee;
USE ieee.std_logic_1164.all;

ENTITY OR_gate IS
  PORT (
		a,b:in std_logic;
		rez:out std_logic
    );
END OR_gate;


ARCHITECTURE TypeArchitecture OF OR_gate IS

BEGIN

rez <= a or b;

END TypeArchitecture;



--- and gate


LIBRARY ieee;
USE ieee.std_logic_1164.all;

ENTITY and_gate IS
  PORT (
 a,b :in std_logic;
 c: out std_logic
    );
END and_gate;


ARCHITECTURE TypeArchitecture OF and_gate IS

BEGIN

c <= a and b;

END TypeArchitecture;



-- frequency divider


LIBRARY ieee;
USE ieee.std_logic_1164.all;
use ieee.std_logic_unsigned.all;

ENTITY FrequencyDivider IS
  PORT (
Clock: in std_logic;
		reset: in std_logic;
		clk_1hz: out std_logic
    );
END FrequencyDivider;


ARCHITECTURE TypeArchitecture OF FrequencyDivider IS


BEGIN

--64 HZ
process (clock)
	variable  var: std_logic_vector  (5 downto 0) := (others =>'0');
	begin
		if rising_edge (clock) then
			if reset='0' 
				then var:=(others=>'0');
			else
				var:=var+1;
			end if;
		end if;
	clk_1hz <= var(5);
end process;

	
END TypeArchitecture;

// VHDL entity RegistruButtons, as the project stores it:
LIBRARY ieee;
USE ieee.std_logic_1164.all;

ENTITY RegistruButtons IS
  PORT (
load,clk:in std_logic;
  		data:in std_logic_vector (8 downto 0);
  		q:out std_logic_VECTOR (8 downto 0 )

    );
END RegistruButtons;

ARCHITECTURE TypeArchitecture OF RegistruButtons IS

BEGIN

	process (clk)
	variable reg: std_Logic_vector (8 downto 0) := (others => '0');
	begin
	if rising_edge(clk) then
		if (load ='1') then
			reg:=data;
		else 
			reg:=reg;
		end if;
	end if;
 q<= reg;
 end process;


END TypeArchitecture;

// VHDL entity BUTTONmaibun, as the project stores it:
LIBRARY ieee;
USE ieee.std_logic_1164.all;

ENTITY BUTTONmaibun IS
  PORT (
   reset,MANUAL:in STD_LOGIC;
  t30,t40,t60,t90 :in STD_LOGIC;
  r800,r1000,r1200:in STD_LOGIC;
  SPALARE_RAPIDA,CAMASI,ANTIALERGIC,CULORI_INCHISE,RUFE_MURDARE,DOOR:in STD_LOGIC;
  prespalare,clatire :in STD_LOGIC;
  v : out STD_LOGIC_VECTOR(8 downto 0)
    );
END BUTTONmaibun;

ARCHITECTURE TypeArchitecture OF BUTTONmaibun IS
signal doorandmanual: std_logic;
signal doorandautomat: std_logic;
--signal vector:std_logic_vector (8 downto 0) := (others =>'0');
BEGIN
--process(reset,t30,t40,t60,t90,r800,r1000,r1200,prespalare,clatire,SPALARE_RAPIDA,CAMASI,ANTIALERGIC,CULORI_INCHISE,RUFE_MURDARE,DOOR,MANUAL,Anulare_Prespalare,Anulare_clatire)
--begin
doorandmanual <= door and manual;
doorandautomat <= door and (not manual);

v(0) <= ((doorandmanual and t30) or (doorandautomat and spalare_rapida)) and (not RESET) ;
v(1) <= ((doorandmanual and t40) or (doorandautomat and (culori_inchise or rufe_murdare))) and (not RESET) ;
v(2) <= ((doorandmanual and t60) or (doorandautomat and camasi)) and (not RESET) ;
v(3) <= ((doorandmanual and t90) or (doorandautomat and antialergic)) and (not RESET);
v(4) <= ((doorandmanual and r800) or (doorandautomat and camasi)) and (not RESET);
v(5) <= ((doorandmanual and r1000) or (doorandautomat and (culori_inchise or rufe_murdare)))and (not RESET)  ;
v(6) <= ((doorandmanual and r1200) or (doorandautomat and (antialergic or spalare_rapida)))and (not RESET) ;
v(7) <= ((doorandmanual and prespalare) or (doorandautomat and (rufe_murdare)))and (not RESET) ;
v(8) <= ((doorandmanual and clatire) or (doorandautomat and (culori_inchise or antialergic))) and (not RESET);


end TypeArchitecture;

// VHDL entity newstarter, as the project stores it:
LIBRARY ieee;
USE ieee.std_logic_1164.all;

ENTITY newstarter IS
  PORT (
            v: in std_logic_vector(8 downto 0);
            door,start: in std_logic;
             output1,output2,output3,output4: out std_logic;
             startmasina:out std_logic
    );
END newstarter;



ARCHITECTURE TypeArchitecture OF newstarter IS

signal doorandstart,rot,temp: std_logic;
signal signal1,signal2: std_logic;
signal b1,b2,b3,b4 :std_logic;
signal a1:std_Logic:='0';
signal en:std_logic:='1';
BEGIN


doorandstart<= door and start;
temp <= v(0) or v(1) or v(2) or v(3);
rot<= v(4) or v(5) or v(6);
signal1<= temp and rot;

signal2 <= doorandstart and signal1;




b1<= v(0) or v(1) or v(2) or v(3);
b2<= (not v(2) ) and v(3);
b3<= v(1) or v(2);
b4<= v(2) or v(0);

output1<= b1;
output2<=b2;
output3<=b3;
output4<=b4;
process (signal1,start)
begin
if (signal1='1' and start='1' and en='1')then
a1<='1';
en<='0';
end if;
end process;
startmasina<=a1;
END TypeArchitecture;

// VHDL entity mux_12to1, as the project stores it:
library ieee;
use ieee.std_logic_1164.all;

entity mux_12to1 is
  port (
  enable:in std_logic ;
    sel : in std_logic_vector(4 downto 0);
    o : out std_logic_vector(12 downto 0)
  );
end entity mux_12to1;

architecture behavioral of mux_12to1 is
  signal I11: std_logic_vector (12 downto 0):="0100110101011"; 
  signal I10: std_logic_vector (12 downto 0):="0110000000011";
  signal I9: std_logic_vector (12 downto 0):="0111001011011";
  
  signal I8: std_logic_vector (12 downto 0):="0100110111111";
  signal I7: std_logic_vector (12 downto 0):="0110000010111";
  signal I6: std_logic_vector (12 downto 0):="0111001101111";
  
  signal I5: std_logic_vector (12 downto 0):="0100111100111";
  signal I4: std_logic_vector (12 downto 0):="0110000111111";
  signal I3: std_logic_vector (12 downto 0):="0111010010111";
  
  signal I2: std_logic_vector (12 downto 0):="0101000100011";
  signal I1: std_logic_vector (12 downto 0):="0110001111011";
  signal I0: std_logic_vector (12 downto 0):="0111011010011";
  
  signal I: std_logic_vector (12 downto 0):= "0000000000000";
  signal copy: std_logic_vector(12 downto 0):= "0000000000000";
begin
  process (sel,enable,copy)
  begin
 if enable ='1' then
    case sel is
      when "00001" =>
        copy <= I11;
      when "01001" =>
        copy <= I10;
      when "10001" =>
        copy <= I10;
      when "11001" =>
        copy <= I9;
        
      when "00010" =>
       copy <= I8;
      when "01010" =>
        copy <= I7;
      when "10010" =>
        copy <= I7;
      when "11010" =>
        copy <= I6;
        
      when "00011" =>  
        copy <= I5;
      when "01011" =>
        copy <= I4;
      when "10011" =>
        copy <= I4;
      when "11011" =>
        copy <= I3;

      when "00100"=>
      copy <= I2;
      when "01100" =>
      copy <= I1;
      when "10100" =>
      copy <= I1;
      when "11100" =>
      copy <=I0 ;
when others =>
copy <= I;  
    end case;
    else
    copy<=I;
    end if;
      O <= copy;  
  end process;
  
end architecture behavioral;

// VHDL entity newtop, as the project stores it:
LIBRARY ieee;
USE ieee.std_logic_1164.all;

ENTITY newtop IS
  PORT (
  rst,manualt,startt ,clockt, anulare_prespalare,anulare_clatire,tt30,tt40,tt60,tt90,rr800,rr1000,rr1200,tspalare_rapida,tcamasi,tantialergic,tculori_inchise,trufe_murdare,tdoor,tprespalare,tclatire: in std_logic;
  Q: out std_logic_vector(12 downto 0)
    );
END newtop;


ARCHITECTURE TypeArchitecture1 OF newtop IS

component BUTTONmaibun IS
  PORT (
   reset,MANUAL,t30,t40,t60,t90 ,r800,r1000,r1200,SPALARE_RAPIDA,CAMASI,ANTIALERGIC,CULORI_INCHISE,RUFE_MURDARE,DOOR,prespalare,clatire :in STD_LOGIC;
  v : out STD_LOGIC_VECTOR(8 downto 0)
    );
END component;

component mux_12to1 is 
  port (
  enable:in std_logic ;
    sel : in std_logic_vector(3 downto 0);
    o : out std_logic_vector(12 downto 0)
  );
end component;

component newstarter IS
  PORT (
            v: in std_logic_vector(8 downto 0);
            door,start: in std_logic;
             output1,output2,output3,output4 : out std_logic
    );
END component;

component RegistruButtons IS
  PORT (
load,clk:in std_logic;
  		data:in std_logic_vector (8 downto 0);
  		q:out std_logic_VECTOR (8 downto 0 )

    );
END component;
component Counter13 IS
  PORT (
		Load, Clk_EN, CLK, RST: in std_logic;
		Data: in std_logic_vector(12 downto 0);
		Q: out std_logic_vector(12 downto 0)
  );
END component;
signal o1,o2,o3,o4:std_logic;
signal output_butoane,y:std_logic_vector(8 downto 0);
signal sel: std_logic_vector(3 downto 0);
signal notds,doorandstartt:std_logic;
signal output_mux,final: std_logic_vector(12 downto 0);
BEGIN


doorandstartt <= tdoor and startt;
p1:BUTTONmaibun port map (rst,manualt,tt30,tt40,tt60,tt90,rr800,rr1000,rr1200,tspalare_rapida,tcamasi,tantialergic,tculori_inchise,trufe_murdare,tdoor,tprespalare,tclatire,output_butoane) ;

--p2:RegistruButtons port map(startt,clockt,u,y);
p3:newstarter port map(output_butoane,tdoor,startt,o1,o2,o3,o4);
sel <= output_butoane(7) & output_butoane(8)& o2 & o3;
p4:mux_12to1 port map (o1 ,sel , output_mux);
notds<= not doorandstartt;
p5:counter13 port map(notds,o4,clockt,rst,output_mux,final);
Q<= final;

END TypeArchitecture1;

-----------------------------------------
LIBRARY ieee;
USE ieee.std_logic_1164.all;

ENTITY BUTTONmaibun IS
  PORT (
   reset,MANUAL:in STD_LOGIC;
  t30,t40,t60,t90 :in STD_LOGIC;
  r800,r1000,r1200:in STD_LOGIC;
  SPALARE_RAPIDA,CAMASI,ANTIALERGIC,CULORI_INCHISE,RUFE_MURDARE,DOOR:in STD_LOGIC;
  prespalare,clatire :in STD_LOGIC;
  v : out STD_LOGIC_VECTOR(8 downto 0)
    );
END BUTTONmaibun;

ARCHITECTURE TypeArchitecture2 OF BUTTONmaibun IS
signal doorandmanual: std_logic;
signal doorandautomat: std_logic;
--signal vector:std_logic_vector (8 downto 0) := (others =>'0');
BEGIN
--process(reset,t30,t40,t60,t90,r800,r1000,r1200,prespalare,clatire,SPALARE_RAPIDA,CAMASI,ANTIALERGIC,CULORI_INCHISE,RUFE_MURDARE,DOOR,MANUAL,Anulare_Prespalare,Anulare_clatire)
--begin
doorandmanual <= door and manual;
doorandautomat <= door and (not manual);

v(0) <= ((doorandmanual and t30) or (doorandautomat and spalare_rapida)) and (not RESET) ;
v(1) <= ((doorandmanual and t40) or (doorandautomat and (culori_inchise or rufe_murdare))) and (not RESET) ;
v(2) <= ((doorandmanual and t60) or (doorandautomat and camasi)) and (not RESET) ;
v(3) <= ((doorandmanual and t90) or (doorandautomat and antialergic)) and (not RESET);
v(4) <= ((doorandmanual and r800) or (doorandautomat and camasi)) and (not RESET);
v(5) <= ((doorandmanual and r1000) or (doorandautomat and (culori_inchise or rufe_murdare)))and (not RESET)  ;
v(6) <= ((doorandmanual and r1200) or (doorandautomat and (antialergic or spalare_rapida)))and (not RESET) ;
v(7) <= ((doorandmanual and prespalare) or (doorandautomat and (rufe_murdare)))and (not RESET) ;
v(8) <= ((doorandmanual and clatire) or (doorandautomat and (culori_inchise or antialergic))) and (not RESET);
end TypeArchitecture2;

library ieee;
use ieee.std_logic_1164.all;

entity mux_12to1 is
  port (
  enable:in std_logic ;
    sel : in std_logic_vector(3 downto 0);
    o : out std_logic_vector(12 downto 0)
  );
end entity mux_12to1;

architecture behavioral of mux_12to1 is
  signal I11: std_logic_vector (12 downto 0):="0111000111101";
  signal I10: std_logic_vector (12 downto 0):="0110000000011";
  signal I9: std_logic_vector (12 downto 0):="0111001011011";
  signal I8: std_logic_vector (12 downto 0):="0100110111111";
  signal I7: std_logic_vector (12 downto 0):="0110000010111";
  signal I6: std_logic_vector (12 downto 0):="0111001101111";
  signal I5: std_logic_vector (12 downto 0):="0100111100111";
  signal I4: std_logic_vector (12 downto 0):="0110000111111";
  signal I3: std_logic_vector (12 downto 0):="0111010010111";
  signal I2: std_logic_vector (12 downto 0):="0101000100011";
  signal I1: std_logic_vector (12 downto 0):="0110001111011";
  signal I0: std_logic_vector (12 downto 0):="0111011010011";
  signal I: std_logic_vector (12 downto 0):= "0000000000000";
  signal copy: std_logic_vector(12 downto 0):= "0000000000000";
begin
  process (sel,enable,copy)
  begin
 if enable ='1' then
    case sel is
      when "0000" =>
        copy <= I11;
      when "0100" =>
        copy <= I10;
      when "1000" =>
        copy <= I10;
      when "1100" =>
        copy <= I9;
        
      when "0001" =>
       copy <= I8;
      when "0101" =>
        copy <= I7;
      when "1001" =>
        copy <= I7;
      when "1101" =>
        copy <= I6;
        
      when "0010" =>  
        copy <= I5;
      when "0110" =>
        copy <= I4;
      when "1010" =>
        copy <= I4;
      when "1110" =>
        copy <= I3;

      when "0011"=>
      copy <= I2;
      when "0111" =>
      copy <= I1;
      when "1011" =>
      copy <= I1;
      when "1111" =>
      copy <=I0 ;

when others =>
copy <= I;
             O <= copy;     
    end case;
      O <= copy;  
    end if;
      O <= copy;  
  end process;
end architecture behavioral;


LIBRARY ieee;
USE ieee.std_logic_1164.all;

ENTITY newstarter IS
  PORT (
            v: in std_logic_vector(8 downto 0);
            door,start: in std_logic;
             output1,output2,output3,output4 : out std_logic
    );
END newstarter;



ARCHITECTURE TypeArchitecture OF newstarter IS

signal doorandstart,rot,temp: std_logic;
signal signal1,signal2: std_logic;
signal a1,a2,a3,b1,b2,b3 :std_logic;
BEGIN


doorandstart<= door and start;
temp <= v(0) or v(1) or v(2) or v(3);
rot<= v(4) or v(5) or v(6);
signal1<= temp and rot;
signal2 <= doorandstart and signal1;

--a1 <= v(0) and signal2;
--a2 <= v(1) and signal2;
--a3 <= v(3) and signal2;

b1<= v(0) or v(1) or v(2);
b2<= v(0) nor v(1);
b3<= v(0) nor v(2);

output1<= b1;
output2<=b2;
output3<=b3;
output4<= signal2;
END TypeArchitecture;




LIBRARY ieee;
USE ieee.std_logic_1164.all;

ENTITY RegistruButtons IS
  PORT (
load,clk:in std_logic;
  		data:in std_logic_vector (8 downto 0);
  		q:out std_logic_VECTOR (8 downto 0 )

    );
END RegistruButtons;

ARCHITECTURE TypeArchitecture4 OF RegistruButtons IS

BEGIN

	process (clk)
	variable reg: std_Logic_vector (8 downto 0) := (others => '0');
	begin
	if rising_edge(clk) then
		if (load ='1') then
			reg:=data;
		else 
			reg:=reg;
		end if;
	end if;
 q<= reg;
 end process;


END TypeArchitecture4;

LIBRARY ieee;
USE ieee.std_logic_1164.all;

use IEEE.STD_LOGIC_UNSIGNED.ALL;

ENTITY Counter13 IS
  PORT (
		Load, Clk_EN, CLK, RST: in std_logic;
		Data: in std_logic_vector(12 downto 0);
		Q: out std_logic_vector(12 downto 0)
  );
END Counter13;

ARCHITECTURE TypeArchitecture5 OF Counter13 IS

signal count: std_logic_vector(12 downto 0) := (others => '0');

BEGIN
	
	process (CLK, RST)
	begin
		if RST = '1' then
			count <= (others => '0'); -- Reset the counter to 0
		elsif rising_edge(CLK) then
			if Load = '1' then
				count <= Data;
			else 
				if Clk_EN = '1' then
					count <= count - 1;
				else
					count <= count;
				end if;
			end if;
		end if;
		
		Q <= count;
	end process;

END TypeArchitecture5;

// VHDL entity SSD, as the project stores it:
library IEEE;
use IEEE.STD_LOGIC_1164.ALL;
use IEEE.STD_LOGIC_UNSIGNED.ALL;

entity SSD is
    Port (
        clk : in STD_LOGIC;
        d0 : in STD_LOGIC_VECTOR (3 downto 0);
        d1 : in STD_LOGIC_VECTOR (3 downto 0);
        d2 : in STD_LOGIC_VECTOR (3 downto 0);
        d3 : in STD_LOGIC_VECTOR (3 downto 0);
        an : out STD_LOGIC_VECTOR (7 downto 0);
        cat : out STD_LOGIC_VECTOR (6 downto 0)
    );
end SSD;

architecture Behav of SSD is
    signal count : std_logic_vector(15 downto 0);
    signal input_decoder : std_logic_vector(3 downto 0);
begin

    -- Counter process
    process(clk, count)
    begin
        if rising_edge(clk) then
            count <= count + 1;
        end if;
    end process;

    -- ANOZI process
    process(count)
    begin
        case count(15 downto 14) is
            when "00" => an <= "00010000";
            when "01" => an <= "00100000";
            when "10" => an <= "01000000";
            when others => an <= "10000000";
        end case;
    end process;

    -- Decoder process
    process(count, d0, d1, d2, d3)
    begin
        case count(15 downto 14) is
            when "00" => input_decoder <= d0;
            when "01" => input_decoder <= d1;
            when "10" => input_decoder <= d2;
            when others => input_decoder <= d3;
        end case;
    end process;

    -- Output process
    process(input_decoder)
    begin
        case input_decoder is
      when "0000" => cat <= "1111110";
      when "0001" => cat <= "0110000";
      when "0010" => cat <= "1101101";
      when "0011" => cat <= "1111001";
      when "0100" => cat <= "0110011";
      
      when "0101" => cat <= "1011011";
      when "0110" => cat <= "1011111";
      
      when "0111" => cat <= "1110000";
      when "1000" => cat <= "1111111";
      when "1001" => cat <= "1111011";
      when others => cat <= "0000000";
        end case;
    end process;

end Behav;
